# Fritzing sketch mainboard (saved by Fritzing 0.9.4)
circuit board: 7.9cm x 7.9cm
breadboards: 1

parts:
  OXY = Header 2 [package=molex-1x2_lock]
  IC2_PWR = TL074 Quad Opamp (Movable) [package="DIP (Dual Inline)"]  # not connected
  IC2_B = TL074 Quad Opamp (Movable) [package="DIP (Dual Inline)"]  # not connected
  IC2_C = TL074 Quad Opamp (Movable) [package="DIP (Dual Inline)"]  # not connected
  IC2_D = TL074 Quad Opamp (Movable) [package="DIP (Dual Inline)"]  # not connected
  IC1_PWR = TL074 Quad Opamp (Movable) [package="DIP (Dual Inline)"]  # not connected
  IC1_A = TL074 Quad Opamp (Movable) [package="DIP (Dual Inline)"]  # not connected
  IC1_B = TL074 Quad Opamp (Movable) [package="DIP (Dual Inline)"]  # not connected
  IC1_C = TL074 Quad Opamp (Movable) [package="DIP (Dual Inline)"]  # not connected
  IC1_D = TL074 Quad Opamp (Movable) [package="DIP (Dual Inline)"]  # not connected
  IC1_PWR_2 = TL074 Quad Opamp (Movable) [package="DIP (Dual Inline)"]  # not connected
  IC1_A_2 = TL074 Quad Opamp (Movable) [package="DIP (Dual Inline)"]  # not connected
  IC1_B_2 = TL074 Quad Opamp (Movable) [package="DIP (Dual Inline)"]  # not connected
  IC1_C_2 = TL074 Quad Opamp (Movable) [package="DIP (Dual Inline)"]  # not connected
  IC1_D_2 = TL074 Quad Opamp (Movable) [package="DIP (Dual Inline)"]  # not connected
  Arduino_Nano = Arduino Nano (Rev3.0)
  BAT_18650 = 18650 battery holder [package=battery-18650-kit]
  OUT- = rounded female pin header, 1 pin [form="♀ (female rounded)"]
  VIN+ = rounded female pin header, 1 pin [form="♀ (female rounded)"]
  VIN- = rounded female pin header, 1 pin [form="♀ (female rounded)"]
  on/off = Header 2 [package=molex-1x2_lock]
  1N400X = Diode [package=diode-1n4148]
  OLED = female pin header, 4 pins [form="♀ (female)"]
  buz = Header 2 [package=molex-1x2_lock]
  Button = Header 2 [package=molex-1x2_lock]
  ADS_1115 = Adafruit ADS1115 16Bit I2C ADC [part_number="Adafruit #1085"]
  OUT+ = rounded female pin header, 1 pin [form="♀ (female rounded)"]

nets:
  N1: OXY.1, ADS_1115.AIN1
  N2: OXY.2, ADS_1115.AIN0
  GND: Arduino_Nano.GND, OUT-.pin1, OLED.pin2, buz.1, Button.1, ADS_1115.GND
  N3: Arduino_Nano.D8, Button.2
  N4: Arduino_Nano.D9, buz.2
  VIN: Arduino_Nano.VIN, OLED.pin1, ADS_1115.VDD, OUT+.pin1
  N5: Arduino_Nano.A5, OLED.pin3, ADS_1115.SCL
  N6: Arduino_Nano.A4, OLED.pin4, ADS_1115.SDA
  N7: Arduino_Nano.A0, VIN+.pin1, on/off.1
  N8: BAT_18650.+, on/off.2
  N9: BAT_18650.-, 1N400X.C
  N10: VIN-.pin1, 1N400X.A

notes:
  usb →
  MT3608 DC-DC Booster
  v1.1
  Output = 5V
  GND
  VIN
  SCL
  SDA
  AIN0
  AIN1
  AIN2
  AIN3
  5V
  A5
  A4
  +
  -
  A3
  A2
  A1
  A0
  D2
  D7
  D8
  D4
  D3
  D9
  D6
  D5
  Wouter D' Haeseleer
  Nitrox analyzer - 08 / 12 / 2020
  Oxygen Analyzer
  Use with 8-13mV
  oxygen sensor in air

custom parts:
  TL074 Quad Opamp (Movable): Quadruple Operational Amplifier (Opamp)
  TL074 Quad Opamp (Movable): Quadruple Operational Amplifier (Opamp)
  TL074 Quad Opamp (Movable): Quadruple Operational Amplifier (Opamp)
  TL074 Quad Opamp (Movable): Quadruple Operational Amplifier (Opamp)
  TL074 Quad Opamp (Movable): Quadruple Operational Amplifier (Opamp)
  18650 battery holder: 18650 Battery Holder
  Adafruit ADS1115 16Bit I2C ADC: For microcontrollers without an analog-to-digital converter or when you want a higher-precision ADC, the ADS1115 provides 16-bit precision at 860 samples/second over I2C. The chip can be configured as 4 single-ended input channels, or two differential channels. As a nice bonus, it even includes a programmable gain amplifier, up to x16, to help boost up smaller single/differential signals to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

// code stored in the sketch: Nitrox_wouter.ino

/*****************************************************************************
 * 
 * (c) 2020 Wouter D'Haeseleer <wouter@netdata.be>
 * 
 * o2 analyser - gasblender.org
 * source code derivated from ej's o2 oled analyzer - v0.21 (http://ejlabs.net/arduino-oled-nitrox-analyzer)  
 * 
 * License  
 * -------    
 * This program is free software: you can redistribute it and/or modify    
 * it under the terms of the GNU General Public License as published by    
 * the Free Software Foundation, either version 3 of the License, or    
 * (at your option) any later version.
 *     
 *     This program is distributed in the hope that it will be useful,    
 *     but WITHOUT ANY WARRANTY; without even the implied warranty of
 *     MERCHANTABILITY or FITNESS FOR A PARTICULAR PURPOSE.  See the    
 *     GNU General Public License for more details.
 *         
 *         You should have received a copy of the GNU General Public License    
 *         along with this program.  If not, see <http://www.gnu.org/licenses/>.
 *         
 *****************************************************************************/

#include <SPI.h>
#include <Wire.h>
#include <EEPROM.h>
#include <Adafruit_ADS1015.h>
#include "RunningAverage.h"
#include <Arduino.h>
#include <U8x8lib.h>
#include <avr/wdt.h>

#define RA_SIZE 25
RunningAverage RA(RA_SIZE);
RunningAverage battVolt(20);

Adafruit_ADS1115 ads(0x48);

U8X8_SH1106_128X64_NONAME_HW_I2C u8x8(/* reset=*/ U8X8_PIN_NONE);


double barsize = RA_SIZE / 16.0 ;
double calibrationv = 0;
float multiplier;
byte previous = HIGH;
unsigned long firstTime; // how long since the button was first pressed
int battPcrt = 0;
int active = 0;
int bootcounter = 0;
int toggle = 0;
int errorState = 0;
int page = 0;
double result_max = 0;
uint8_t lijn_onder[8] = { 128,128,128,128,128,128,128,128};
uint8_t lijn_boven[8] = { 1,1,1,1,1,1,1,1};
uint8_t lijn_links[8] = { 255,0,0,0,0,0,0,0};
uint8_t lijn_rechts[8] = { 0,0,0,0,0,0,0,255};

#define milivolt_low_error 6
#define milivolt_high_error 80

#define buttonPin 8

//const int buzzer = 8; // buzzer
//const int ledPin = 13; // led
#define cal_holdTime 2000 // 2 sec button hold to calibration

#define mod_holdTime 3000 // 3 sec hold to po2 mod change
#define max_holdtime 4000 // 4 sec hold to reset max o2 result
long millis_held;    // How long the button was held (milliseconds)
long secs_held;      // How long the button was held (seconds)
long prev_secs_held; // How long the button was held in the previous check

/*
  Calculate MOD (Maximum Operating Depth)
*/
#define max_po1 1.40


float cal_mod (float percentage, float ppo2 = 1.4) {
  return 10 * ( (ppo2 / (percentage / 100)) - 1 ); 
}

//not used for gasblender 1.0
/*
void beep(int x = 1) { // make beep for x time
  //digitalWrite(ledPin, HIGH); // led blink disable for battery save
  for (int i = 0; i < x; i++) {
    tone(buzzer, 2800, 100);
    delay(200);
  }
  //digitalWrite(ledPin, LOW);
  noTone(buzzer);
}
*/

void read_sensor(int adc = 0) {
  int16_t millivolts = 0;
  millivolts = ads.readADC_Differential_0_1();
  millivolts = abs(millivolts);
  /* debug  erics */
   // Serial.print("read_sensor o2: ");
   // Serial.print(millivolts);
   // Serial.print("\n");
  /* */
  
 
  RA.addValue(millivolts);
  wdt_reset();
}

void setup(void) {
  
  Serial.begin(9600);
  Serial.print("Running: Setup\n");

  page = EEPROMReadInt(1);

  // Init 
  u8x8.begin();
  ads.begin(); // ads1115 start
  RA.clear();
  battVolt.clear();


  /* power saving stuff for battery power */
  // Disable ADC
  // ADCSRA = 0;
  // Disable the analog comparator by setting the ACD bit
  // (bit 7) of the ACSR register to one.
  ACSR = B10000000;
  // Disable digital input buffers on all analog input pins
  DIDR0 = DIDR0 | B00111111;

  //ads.setGain(GAIN_TWO);
  //multiplier = 0.0625F;
               
  //ads.setGain(GAIN_EIGHT);u8x8.clearDisplay();
  //multiplier = 0.015625F;

  ads.setGain(GAIN_SIXTEEN);
  multiplier = 0.0078125F; 

  pinMode(buttonPin, INPUT);

  batteryMonitor();

 
  u8x8.setFont(u8x8_font_profont29_2x3_r);
  //u8x8.setFont(u8x8_font_torussansbold8_r);
  u8x8.setInverseFont(1);
  //u8x8.drawString(0,0,"12345678");
  u8x8.drawString(0,0," WOUTER ");
  u8x8.setInverseFont(0);
  u8x8.setFont(u8x8_font_chroma48medium8_r);
  u8x8.drawString(3,5,"NITROX v1.0");
  u8x8.drawString(6,7,"2020");

  
  delay(2000);
  //EEPROMWriteInt(1, 0);
  
  //calibrationv = EEPROMReadInt(0);

  

  //}
  u8x8.clearDisplay();
  Serial.print("Setup finished\n");



  //beep(1);
}

void EEPROMWriteInt(int p_address, int p_value)
{
  /*  
    Serial.print("EEPROMWriteInt ");
    Serial.print(p_address);
    Serial.print(" : ");
    Serial.print(p_value);
    Serial.print("\n");
  */
  byte lowByte = ((p_value >> 0) & 0xFF);
  byte highByte = ((p_value >> 8) & 0xFF);

  EEPROM.write(p_address, lowByte);
  EEPROM.write(p_address + 1, highByte);
}

unsigned int EEPROMReadInt(int p_address)
{
  byte lowByte = EEPROM.read(p_address);
  byte highByte = EEPROM.read(p_address + 1);

  return ((lowByte << 0) & 0xFF) + ((highByte << 8) & 0xFF00);
}

int calibrate(int x) {
  /* */
    Serial.print("calibrate:");
    Serial.print(x);
    Serial.print("\n");
  /* */

  RA.clear();
  u8x8.clearDisplay();
  u8x8.setFont(u8x8_font_chroma48medium8_r);
  u8x8.drawString(0,0,"AUTO CALIBRATING");


  
  u8x8.setFont(u8x8_font_chroma48medium8_r);


  u8x8.drawTile(0,3, 1, lijn_onder);
  u8x8.drawTile(1,3, 1, lijn_onder);
  u8x8.drawTile(2,3, 1, lijn_onder);  
  u8x8.drawTile(3,3, 1, lijn_onder);
  u8x8.drawTile(4,3, 1, lijn_onder);  
  u8x8.drawTile(5,3, 1, lijn_onder);
  u8x8.drawTile(6,3, 1, lijn_onder);
  u8x8.drawTile(7,3, 1, lijn_onder);
  u8x8.drawTile(8,3, 1, lijn_onder);
  u8x8.drawTile(9,3, 1, lijn_onder);
  u8x8.drawTile(10,3, 1, lijn_onder);
  u8x8.drawTile(11,3, 1, lijn_onder);
  u8x8.drawTile(12,3, 1, lijn_onder);
  u8x8.drawTile(13,3, 1, lijn_onder);
  u8x8.drawTile(14,3, 1, lijn_onder);
  u8x8.drawTile(15,3, 1, lijn_onder);

  u8x8.drawTile(0,4, 1, lijn_links);
  u8x8.drawTile(15,4, 1, lijn_rechts);

  u8x8.drawTile(0,5, 1, lijn_boven);
  u8x8.drawTile(1,5, 1, lijn_boven);
  u8x8.drawTile(2,5, 1, lijn_boven);  
  u8x8.drawTile(3,5, 1, lijn_boven);
  u8x8.drawTile(4,5, 1, lijn_boven);  
  u8x8.drawTile(5,5, 1, lijn_boven);
  u8x8.drawTile(6,5, 1, lijn_boven);
  u8x8.drawTile(7,5, 1, lijn_boven);
  u8x8.drawTile(8,5, 1, lijn_boven);
  u8x8.drawTile(9,5, 1, lijn_boven);
  u8x8.drawTile(10,5, 1, lijn_boven);
  u8x8.drawTile(11,5, 1, lijn_boven);
  u8x8.drawTile(12,5, 1, lijn_boven);
  u8x8.drawTile(13,5, 1, lijn_boven);
  u8x8.drawTile(14,5, 1, lijn_boven);
  u8x8.drawTile(15,5, 1, lijn_boven);

  
  //u8x8.drawString(2,4,"[...........");
  //u8x8.drawString(3,5,"..........]");
  u8x8.drawString(2,7,"20.9 oxygen");


  uint8_t middlebar[8] = { 60,60,60,60,60,60,0,0};
  uint8_t firstbar[8] = { 255,60,60,60,60,60,0,0};
  uint8_t lastbar[8] = { 60,60,60,60,60,60,0,255};

  double result;

  
  int bar = 1;
  
  for (int cx = 0; cx <= RA_SIZE; cx++) {
    u8x8.setFont(u8x8_font_chroma48medium8_r);
    
    if(cx >= (barsize*bar)) {

      switch (bar) {
        case 1:
          u8x8.drawTile(bar-1,4, 1, firstbar);
          break;
        case 16:
          u8x8.drawTile(bar-1,4, 1, lastbar);
          break;
        default:
          u8x8.drawTile(bar-1,4, 1, middlebar);
          break;
      }
      bar = bar+1;
    }
    read_sensor(0);
    delay(50);
  }
  result = RA.getAverage();
  result = abs(result);
  //EEPROMWriteInt(x, result); // write to eeprom
  
  Serial.print("Calibration value o2: ");
  Serial.print(result);
  Serial.print("\n");

  if (result <= milivolt_low_error) {
    errorState=1;
    return 0;
  } else {
    u8x8.setFont( u8x8_font_open_iconic_check_8x8);
    u8x8.clearDisplay();
    u8x8.drawString(4,0,"A");
  
    //beep(1);
    delay(500);
    active = 0;
    u8x8.clearDisplay();
    return result;
  }
}

void error(int e) {
  double currentmv = 0;
  double result;
  double mv = 0.0;

  read_sensor(0);
  currentmv = RA.getAverage();
  currentmv = abs(currentmv);
  mv = currentmv * multiplier;
  // Serial.print("mv = ");
  // Serial.print(mv);
  // Serial.print("\n");


  u8x8.setFont( u8x8_font_open_iconic_check_2x2 );
  u8x8.drawString(3,0,"D");
  u8x8.setFont(u8x8_font_chroma48medium8_r);
  u8x8.drawString(7,0,"SENSOR");
  u8x8.drawString(7,1,"ERROR");
    

  u8x8.setInverseFont(1);

  if ( e == 1 ) {
     u8x8.drawString(0,4,"  Voltage LOW   ");
   } else if ( e == 2 ) {
     u8x8.drawString(0,4,"  Voltage High   ");
   } else {
     u8x8.drawString(0,4,"  Unknown Err   ");
   }  
  
  u8x8.setInverseFont(0);

  u8x8.setCursor(4, 7);
  u8x8.print(mv , 1);
  u8x8.print(" mV ");

  if (mv > milivolt_low_error && mv < milivolt_high_error ) {
    errorState = 0;
    calibrationv = 0;
    result_max = 0;
  } 
}

byte countDigits(int num){
  byte count=0;
  while(num){
    num=num/10;
    count++;
  }
  return count;
}

void batteryMonitor() {
  int battVolt_Value = analogRead(A0);
  battVolt.addValue(battVolt_Value * (5.0 / 1023.0));
  float volt = battVolt.getAverage();

  if ( volt >= 4.2 )  {
    battPcrt = 100;
  }
  if ( volt < 4.2 && volt >=  4.1 ) {
    battPcrt = 90;
  }
  if ( volt < 4.1 && volt >=  4.0 ) {
    battPcrt = 80;
  }
  if ( volt < 4.0 && volt >=  3.9 ) {
    battPcrt = 70;
  }
  if ( volt < 3.9 && volt >=  3.8 ) {
    battPcrt = 60;
  }
  if ( volt < 3.7 && volt >=  3.6 ) {
    battPcrt = 20;
  }
  if ( volt < 3.6 ) {
    battPcrt = 0;
  }
}

void analysing(int x, int cal) {
  double currentmv = 0;
  double result;
  double mv = 0.0;
  int mod = 0;
  

  read_sensor(0);
  currentmv = RA.getAverage();
  currentmv = abs(currentmv);

  result = (currentmv / cal) * 20.9;

  mv = currentmv * multiplier;


  //Serial.print(" mv = ");
  //Serial.print(mv);
  //Serial.print("\n");
  if (result > 99.9) result = 99.9;


  if (mv < milivolt_low_error || result <= 0 ) {
    u8x8.clearDisplay();
    errorState=1;
  } else if ( mv > milivolt_high_error ) {
    u8x8.clearDisplay();
    errorState=2; 
  } else {
    u8x8.setFont(u8x8_font_chroma48medium8_r);

    if (result >= result_max) {
      result_max = result;
    }




    if ( page == 0 ) {

      u8x8.setFont(u8x8_font_inb33_3x6_n);
      //u8x8.setFont(u8x8_font_inr46_4x8_n);
      
      u8x8.setCursor(2, 0);
      u8x8.print((float) result, 1);

      u8x8.setFont(u8x8_font_chroma48medium8_r);

 
      u8x8.setCursor(0, 6);
      u8x8.print("Max = ");
      u8x8.print(result_max, 1);
      u8x8.print(" %");
      u8x8.setCursor(0, 7);
      u8x8.print("Mod = ");
      u8x8.print(floor(cal_mod(result, max_po1)),0);
      u8x8.print(" (1.4)");

      // u8x8.setCursor(6, 7);
      //u8x8.print(String((float) mv , 1).length());      
      
    }

    
    if ( page == 1 ) {

      u8x8.setFont(u8x8_font_inb33_3x6_n);
      //u8x8.setFont(u8x8_font_inr46_4x8_n);
      
      u8x8.setCursor(2, 0);
      u8x8.print((float) result, 1);

      u8x8.setFont(u8x8_font_chroma48medium8_r);

 
      u8x8.setCursor(0, 6);
      u8x8.print("Max = ");
      u8x8.print(result_max, 1);
      u8x8.print(" %");
      u8x8.setCursor(0, 7);
      u8x8.print("Mod = ");
      u8x8.print(floor(cal_mod(result, 1.6)),0);
      u8x8.print(" (1.6)");

      // u8x8.setCursor(6, 7);
      //u8x8.print(String((float) mv , 1).length());      
      
    }

        if ( page == 2 ) {

      u8x8.setFont(u8x8_font_inb33_3x6_n);
      //u8x8.setFont(u8x8_font_inr46_4x8_n);
      
      u8x8.setCursor(2, 0);
      u8x8.print((float) result, 1);

      u8x8.setFont(u8x8_font_chroma48medium8_r);

 
      u8x8.setCursor(0, 6);
      u8x8.print("Max = ");
      u8x8.print(result_max, 1);
      u8x8.print(" %");
      u8x8.setCursor(0, 7);
      u8x8.print("Mod = ");
      u8x8.print(floor(cal_mod(result, 2.0)),0);
      u8x8.print(" (2.0)");

      // u8x8.setCursor(6, 7);
      //u8x8.print(String((float) mv , 1).length());      
      
    }

    // Display Only large result
    if ( page == 3 ) {

       u8x8.setFont(u8x8_font_inb33_3x6_n);
      //u8x8.setFont(u8x8_font_inr46_4x8_n);
      
      u8x8.setCursor(2, 0);
      u8x8.print((float) result, 1);

      u8x8.setFont(u8x8_font_chroma48medium8_r);

 
      u8x8.setCursor(4, 7);
      u8x8.print(mv , 1);
      u8x8.print(" mV ");

      // u8x8.setCursor(6, 7);
      //u8x8.print(String((float) mv , 1).length());      
      
    }

    if ( page == 4 ) {

      
      u8x8.setFont(u8x8_font_open_iconic_embedded_4x4);

      u8x8.setCursor(2, 1);
      u8x8.print("I");

      u8x8.setFont(u8x8_font_profont29_2x3_r);

      u8x8.setCursor(4, 5);
      u8x8.print(battPcrt);
      u8x8.print(" %  ");

      u8x8.setFont(u8x8_font_chroma48medium8_r);
      u8x8.setCursor(8, 2);
      u8x8.print(battVolt.getAverage() , 1);
      u8x8.print(" Volt");

      /*
      u8x8.setCursor(0, 1);
      u8x8.print("Battery");
      u8x8.setCursor(0, 3);
      u8x8.print(battPcrt);
      u8x8.print(" %  ");

      u8x8.setCursor(0, 5);
      u8x8.print(battVolt.getAverage() , 2);
      u8x8.print(" Volt  ");  
      */    
      
    }

    /*
    if ( page == 2 ) {
 
      //u8x8.setFont(u8x8_font_inb46_4x8_n);
      //u8x8.setFont(u8x8_font_inr46_4x8_n);
      
      u8x8.setCursor(0, 0);
      u8x8.print((float) result, 1);
    
      
    }
    */
    
    //if (toggle == 0) {
    //  toggle=1;
    //  u8x8.setFont(u8x8_font_open_iconic_embedded_1x1);
    //  u8x8.drawString(15,7,"O");
    //} else {
    //  toggle=0; 
    //  u8x8.setFont(u8x8_font_open_iconic_embedded_1x1);
    //  u8x8.drawString(15,7," ");
    //}

    //u8x8.setCursor(9, 6);
    //u8x8.print("m");

    //display.print(F("%   "));
    //display.setCursor(75,31);
    //display.print(mv, 2);
    //display.println(F("mv"));

    //display.setCursor(115, 29);
    //display.setTextColor(WHITE);
    //if (active % 4) {
    //  display.print(F("."));
    //  //pour eviter un overflow du int ...
    // }
    // else {
    //   display.print(F("o"));          
    // }
    
    //display.setTextColor(WHITE);
    //display.setCursor(0, 40);
    //display.print(F("pO2 "));
    //display.print(max_po1, 1);
    //display.print(F("  |"));
    //display.print(max_po2, 1);
    //display.print(F(" MOD"));

    //display.setTextSize(2);
    //display.setCursor(0, 50);
    //display.print(cal_mod(result, max_po1), 1);
    //display.print(F("|"));
    //display.print(cal_mod(result, max_po2), 1);
    //display.println(F("m"));

    
    // menu - not used for gasblender 1.0
    /*
    if (secs_held < 5 && active > 16) {
      display.setTextSize(2);
      display.setCursor(0, 31);
      display.setTextColor(BLACK, WHITE);
      if (secs_held >= cal_holdTime && secs_held < mod_holdTime) {
        display.print(F("   CAL    "));
      }
      if (secs_held >= mod_holdTime && secs_held < max_holdtime) {
        display.print(F("   PO2    "));
      }
      if (secs_held >= max_holdtime && secs_held < 10) {
        display.print(F("   MAX    "));
      }
    }
    */
  }
  //display.display();
}


void max_clear() {
  result_max = 0;
  //display.clearDisplay();
  //display.setTextColor(WHITE);
  //display.setCursor(0, 0);
  //display.setTextSize(2);
  //display.println(F("Max result"));
  //display.print(F("cleared"));
  //display.display();
  //beep(1);
  //delay(1000);
  battVolt.clear();
  active = 0;
}



void loop(void) {
  wdt_enable(WDTO_8S);
  batteryMonitor();


  //Serial.print(battVolt.getAverage());
  //Serial.print("\n");
  
 int current = digitalRead(buttonPin);
 
  if (current == HIGH && previous == LOW && (millis() - firstTime) > 200) {
    firstTime = millis();
  }

  millis_held = (millis() - firstTime);
  secs_held = millis_held / 1000;

  if (millis_held > 2) {
    if (current == LOW && previous == HIGH) {
      Serial.print("millis_held = ");
      Serial.print(millis_held);
      Serial.print("\n");
      if (millis_held <= 400) {
        
        page++;
        if ( page >= 5 ) {
          page = 0;
        }

        if ( page != 4 ) { 
          EEPROMWriteInt(1, page);
        }
        
        u8x8.clearDisplay();
      }
      if (millis_held >= 400 && millis_held < mod_holdTime) {
        max_clear();
        calibrationv = calibrate(0);
        Serial.print("Button = Option 2 ================\n");
      }
      if (millis_held >= mod_holdTime && millis_held < max_holdtime) {
        //po2_change();
        Serial.print("Button = Option 3 ================\n");
      }
      if (millis_held >= max_holdtime && millis_held < 10) {
        Serial.print("Button = Option 4 ================\n");
        //max_clear();
      }
    }
  }

  previous = current;
  prev_secs_held = secs_held;

  if ( errorState > 0 ) {
    error(errorState);
  } else { 
    //calibration forced on boot
    if (calibrationv == 0) {
      calibrationv = calibrate(0);
    }

    analysing(0, calibrationv);
  }
  wdt_reset();
  active++;
}
